# Fritzing sketch ATtiny13_blink (saved by Fritzing 0.9.6b)
breadboards: 1

parts:
  R1 = Resistor [tolerance=±5% power=0.25 resistance=220 package=THT]
  U1 = ATTINY13 [package=dip]
  LED1 = LED - 5mm [color="Green (555nm)" current=0.030 package="5 mm [THT]"]
  BAT1 = Battery Holders [package=battcom_20mm_pth]

nets:
  N1: R1.Pin_0, U1.PB4(ADC2)
  N2: R1.Pin_1, LED1.anode
  N3: U1.GND, LED1.cathode, BAT1.-
  N4: U1.VCC, BAT1.+
