# Fritzing sketch ArduinoISP_ATtiny13 (saved by Fritzing 0.9.6b)
breadboards: 1

parts:
  Деталь1 = Arduino Nano (Rev3.0)
  U1 = ATTINY13 [package=dip]
  C1 = Electrolytic Capacitor [capacitance=10µF voltage=35V package="0807 [SMD, electrolytic]"]
  LED1 = LED - 3mm [color="Green (555nm)" current=0.030 package="3 mm [THT]"]
  R1 = Resistor [tolerance=±5% resistance=220 package="0402 [SMD]"]

nets:
  N1: Деталь1.RESET, C1.+
  GND: Деталь1.GND, U1.GND, C1.-, LED1.cathode
  N2: Деталь1.D10, U1.PB5(NRES)
  N3: Деталь1.D11/MOSI, U1.PB0(MOSI)
  N4: Деталь1.D12/MISO, U1.PB1(MISO)
  3V3: Деталь1.3V3, U1.VCC
  N5: Деталь1.D13/SCK, U1.PB2(SCK_ADC1)
  N6: U1.PB4(ADC2), R1.Pin_0
  N7: LED1.anode, R1.Pin_1
