# Fritzing sketch shift_stepper (saved by Fritzing 0.9.6b)
perfboards: 1

parts:
  IC1 = ULN2003A [package="DIP16 [THT]"]
  IC2 = ULN2003A [package="DIP16 [THT]"]
  U1 = 74HC595 [package="DIP16 [THT]"]
  U2 = 74HC595 [package="DIP16 [THT]"]
  WeMos_D1_Mini1 = WeMos D1 Mini  # not connected
  JP1 = Header 1 [package=1x01_offset]
  JP2 = Header 1 [package=1x01_offset]
  JP3 = Header 1 [package=1x01_offset]
  JP4 = Header 1 [package=1x01_offset]
  JP5 = Header 1 [package=1x01_offset]
  JP6 = Header 1 [package=1x01_offset]
  JP7 = Header 1 [package=1x01_offset]
  JP8 = Header 1 [package=1x01_offset]
  JP9 = Header 1 [package=1x01_offset]
  JP10 = Header 1 [package=1x01_offset]
  JP15 = Header 1 [package=1x01_offset]
  JP14 = Header 1 [package=1x01_offset]
  JP13 = Header 1 [package=1x01_offset]
  JP12 = Header 1 [package=1x01_offset]
  JP11 = Header 1 [package=1x01_offset]

nets:
  N1: IC1.In_1, U1.Q7
  N2: IC1.In_2, U1.Q6
  N3: IC1.In_3, U1.Q5
  N4: IC1.In_4, U1.Q4
  N5: IC1.In_5, U1.Q3
  N6: IC1.In_6, U1.Q2
  N7: IC1.In_7, U1.Q1
  GND: IC1.0V, IC2.0V, U1.GND, U2.GND
  VCC: IC1.COM_-_Common, IC2.COM_-_Common, U1.VCC, U2.VCC, JP1.1, JP6.1, JP11.1
  N8: IC1.Out_7, JP10.1
  N9: IC1.Out_6, JP12.1
  N10: IC1.Out_5, JP13.1
  N11: IC1.Out_4, JP14.1
  N12: IC1.Out_3, JP15.1
  N13: IC2.In_1, U2.Q7
  N14: IC2.In_2, U2.Q6
  N15: IC2.In_3, U2.Q5
  N16: IC2.In_4, U2.Q4
  N17: IC2.In_5, U2.Q3
  N18: IC2.In_6, U2.Q2
  N19: IC2.In_7, U2.Q1
  N20: IC2.Out_7, JP2.1
  N21: IC2.Out_6, JP3.1
  N22: IC2.Out_5, JP4.1
  N23: IC2.Out_4, JP5.1
  N24: IC2.Out_3, JP7.1
  N25: IC2.Out_2, JP8.1
  N26: IC2.Out_1, JP9.1

notes:
  XH-2.54-5P?
