# Fritzing sketch shift_stepper_alt (saved by Fritzing 0.9.6b)
perfboards: 1

parts:
  IC2 = ULN2003A [package="DIP16 [THT]"]
  U4 = 74HC595 [package="DIP16 [THT]"]
  IC3 = ULN2003A [package="DIP16 [THT]"]
  U5 = 74HC595 [package="DIP16 [THT]"]
  JP2 = Header 1 [package=1x01_offset]
  JP3 = Header 1 [package=1x01_offset]
  JP4 = Header 1 [package=1x01_offset]
  JP5 = Header 1 [package=1x01_offset]
  JP6 = Header 1 [package=1x01_offset]
  JP7 = Header 1 [package=1x01_offset]
  JP8 = Header 1 [package=1x01_offset]
  JP9 = Header 1 [package=1x01_offset]
  JP10 = Header 1 [package=1x01_offset]
  JP11 = Header 1 [package=1x01_offset]
  JP12 = Header 1 [package=1x01_offset]
  JP13 = Header 1 [package=1x01_offset]
  JP14 = Header 1 [package=1x01_offset]
  JP15 = Header 1 [package=1x01_offset]
  JP16 = Header 1 [package=1x01_offset]
  WeMos_D1_Mini2 = WeMos D1 Mini
  U6 = Voltage Regulator [package=78xxl]  # not connected

nets:
  N1: IC2.In_1, U4.Q7
  N2: IC2.In_2, U4.Q6
  N3: IC2.In_3, U4.Q5
  N4: IC2.In_4, U4.Q4
  N5: IC2.In_5, U4.Q3
  N6: IC2.In_6, U4.Q2
  N7: IC2.In_7, U4.Q1
  GND: IC2.0V, U4.GND, U4.OE, IC3.0V, U5.GND, U5.OE, WeMos_D1_Mini2.G
  VCC: IC2.COM_-_Common, U4.MR, U4.VCC, IC3.COM_-_Common, U5.MR, JP2.1, JP7.1, JP12.1, WeMos_D1_Mini2.5V
  N8: IC2.Out_7, JP11.1
  N9: IC2.Out_6, JP13.1
  N10: IC2.Out_5, JP14.1
  N11: IC2.Out_4, JP15.1
  N12: IC2.Out_3, JP16.1
  N13: U4.SH_CP, U5.SH_CP
  N14: U4.ST_CP, U5.ST_CP, WeMos_D1_Mini2.D8
  N15: U4.DS, U5.Q7'
  N16: IC3.In_1, U5.Q7
  N17: IC3.In_2, U5.Q6
  N18: IC3.In_3, U5.Q5
  N19: IC3.In_4, U5.Q4
  N20: IC3.In_5, U5.Q3
  N21: IC3.In_6, U5.Q2
  N22: IC3.In_7, U5.Q1
  N23: IC3.Out_7, JP3.1
  N24: IC3.Out_6, JP4.1
  N25: IC3.Out_5, JP5.1
  N26: IC3.Out_4, JP6.1
  N27: IC3.Out_3, JP8.1
  N28: IC3.Out_2, JP9.1
  N29: IC3.Out_1, JP10.1
  N30: U5.DS, WeMos_D1_Mini2.D7
