# Fritzing sketch shift_stepper_alt_2 (saved by Fritzing 0.9.6b)
perfboards: 1

parts:
  IC2 = ULN2003A [package="DIP16 [THT]"]
  U4 = 74HC595 [package="DIP16 [THT]"]
  U5 = 74HC595 [package="DIP16 [THT]"]
  JP2 = Header 1 [package=1x01_offset]  # not connected
  JP3 = Header 1 [package=1x01_offset]
  JP4 = Header 1 [package=1x01_offset]
  JP5 = Header 1 [package=1x01_offset]
  JP6 = Header 1 [package=1x01_offset]
  JP7 = Header 1 [package=1x01_offset]  # not connected
  JP8 = Header 1 [package=1x01_offset]
  JP9 = Header 1 [package=1x01_offset]
  JP10 = Header 1 [package=1x01_offset]
  JP11 = Header 1 [package=1x01_offset]  # not connected
  JP12 = Header 1 [package=1x01_offset]  # not connected
  JP13 = Header 1 [package=1x01_offset]
  JP14 = Header 1 [package=1x01_offset]
  JP15 = Header 1 [package=1x01_offset]
  JP16 = Header 1 [package=1x01_offset]
  IC3 = ULN2003A [package="DIP16 [THT]"]

nets:
  N1: IC2.In_1, U4.Q7
  N2: IC2.In_2, U4.Q6
  N3: IC2.In_3, U4.Q5
  N4: IC2.In_4, U4.Q4
  N5: IC2.In_5, U4.Q3
  N6: IC2.In_6, U4.Q2
  N7: IC2.In_7, U4.Q1
  N8: IC2.Out_6, JP13.1
  N9: IC2.Out_5, JP14.1
  N10: IC2.Out_4, JP15.1
  N11: IC2.Out_3, JP16.1
  N12: U5.Q1, IC3.In_7
  N13: U5.Q2, IC3.In_6
  N14: U5.Q3, IC3.In_5
  N15: U5.Q4, IC3.In_4
  N16: U5.Q5, IC3.In_3
  N17: U5.Q6, IC3.In_2
  N18: U5.Q7, IC3.In_1
  N19: JP3.1, IC3.Out_7
  N20: JP4.1, IC3.Out_6
  N21: JP5.1, IC3.Out_5
  N22: JP6.1, IC3.Out_4
  N23: JP8.1, IC3.Out_3
  N24: JP9.1, IC3.Out_2
  N25: JP10.1, IC3.Out_1
