# Fritzing sketch shift_stepper_alt_3 (saved by Fritzing 0.9.6b)
perfboards: 1

parts:
  IC4 = ULN2003A [package="DIP16 [THT]"]
  U6 = 74HC595 [package="DIP16 [THT]"]
  IC5 = ULN2003A [package="DIP16 [THT]"]
  U7 = 74HC595 [package="DIP16 [THT]"]
  WeMos_D1_Mini1 = WeMos D1 Mini  # not connected

nets:
  N1: IC4.In_1, U6.Q6
  N2: IC4.In_2, U6.Q5
  N3: IC4.In_3, U6.Q4
  N4: IC4.In_4, U6.Q3
  N5: IC4.In_5, U6.Q2
  N6: IC4.In_6, U6.Q1
  N7: IC4.In_7, U6.Q0
  N8: U6.Q7, IC5.In_7
  N9: IC5.In_1, U7.Q5
  N10: IC5.In_2, U7.Q4
  N11: IC5.In_3, U7.Q3
  N12: IC5.In_4, U7.Q2
  N13: IC5.In_5, U7.Q1
  N14: IC5.In_6, U7.Q0
