# Fritzing sketch shift_stepper_alt_4c_mod1 (saved by Fritzing 0.9.6b)
perfboards: 1

parts:
  IC4 = ULN2003A [package="DIP16 [THT]"]
  IC5 = ULN2003A [package="DIP16 [THT]"]
  U6 = 74HC595 [package="DIP16 [THT]"]
  U7 = 74HC595 [package="DIP16 [THT]"]
  JP4 = Header 1 [package=1x01_offset]
  JP5 = Header 1 [package=1x01_offset]
  JP6 = Header 1 [package=1x01_offset]
  JP7 = Header 1 [package=1x01_offset]
  JP8 = Header 1 [package=1x01_offset]
  JP9 = Header 1 [package=1x01_offset]
  JP10 = Header 1 [package=1x01_offset]
  JP11 = Header 1 [package=1x01_offset]
  JP12 = Header 1 [package=1x01_offset]
  JP13 = Header 1 [package=1x01_offset]
  JP14 = Header 1 [package=1x01_offset]
  JP15 = Header 1 [package=1x01_offset]
  JP16 = Header 1 [package=1x01_offset]
  JP17 = Header 1 [package=1x01_offset]
  JP3 = Header 1 [package=1x01_offset]
  WeMos_D1_Mini2 = WeMos D1 Mini
  JP18 = Header 1 [package=1x01_offset]
  JP19 = Header 1 [package=1x01_offset]
  JP20 = Header 1 [package=1x01_offset]
  JP21 = Header 1 [package=1x01_offset]
  JP23 = Header 1 [package=1x01_offset]
  JP24 = Header 1 [package=1x01_offset]
  JP25 = Header 1 [package=1x01_offset]
  JP26 = Header 1 [package=1x01_offset]
  JP28 = Header 1 [package=1x01_offset]
  JP29 = Header 1 [package=1x01_offset]
  JP30 = Header 1 [package=1x01_offset]
  JP31 = Header 1 [package=1x01_offset]
  JP32 = Header 1 [package=1x01_offset]
  JP33 = Header 1 [package=1x01_offset]
  JP34 = Header 1 [package=1x01_offset]
  JP35 = Header 1 [package=1x01_offset]

nets:
  N1: IC4.In_1, U6.Q7
  N2: IC4.In_2, U6.Q6
  N3: IC4.In_3, U6.Q5
  N4: IC4.In_4, U6.Q4
  N5: IC4.In_5, U6.Q3
  N6: IC4.In_6, U6.Q2
  N7: IC4.In_7, U6.Q1
  GND: IC4.0V, IC5.0V, U6.GND, U6.OE, U7.GND, U7.OE, WeMos_D1_Mini2.G, JP18.1, JP24.1, JP28.1, JP31.1
  VCC: IC4.COM_-_Common, IC5.COM_-_Common, U6.MR, U6.VCC, U7.MR, U7.VCC, JP8.1, JP13.1, JP3.1, JP19.1, JP21.1, JP32.1, JP34.1
  N8: IC4.Out_7, JP4.1
  N9: IC4.Out_6, JP5.1
  N10: IC4.Out_5, JP6.1
  N11: IC4.Out_4, JP7.1
  N12: IC4.Out_3, JP35.1
  N13: IC4.Out_2, JP9.1
  N14: IC4.Out_1, JP10.1
  N15: IC5.In_1, U7.Q7
  N16: IC5.In_2, U7.Q6
  N17: IC5.In_3, U7.Q5
  N18: IC5.In_4, U7.Q4
  N19: IC5.In_5, U7.Q3
  N20: IC5.In_6, U7.Q2
  N21: IC5.In_7, U7.Q1
  N22: IC5.Out_7, JP11.1
  N23: IC5.Out_6, JP12.1
  N24: IC5.Out_5, JP33.1
  N25: IC5.Out_4, JP14.1
  N26: IC5.Out_3, JP15.1
  N27: IC5.Out_2, JP16.1
  N28: IC5.Out_1, JP17.1
  N29: U6.Q7', U7.DS
  N30: U6.SH_CP, U7.SH_CP, WeMos_D1_Mini2.D5
  N31: U6.ST_CP, U7.ST_CP, WeMos_D1_Mini2.D8
  N32: U6.DS, WeMos_D1_Mini2.D7
  N33: WeMos_D1_Mini2.3V3, JP25.1
  N34: WeMos_D1_Mini2.5V, JP20.1
  N35: WeMos_D1_Mini2.D1, JP23.1
  N36: WeMos_D1_Mini2.D2, JP29.1
  N37: WeMos_D1_Mini2.D3, JP30.1
  N38: WeMos_D1_Mini2.D4, JP26.1
