# Fritzing sketch shift_stepper_alt_4c_mod1_bottom_layer (saved by Fritzing 0.9.6b)
perfboards: 1

parts:
  JP4 = Header 1 [package=1x01_offset]  # not connected
  JP5 = Header 1 [package=1x01_offset]
  JP6 = Header 1 [package=1x01_offset]
  JP7 = Header 1 [package=1x01_offset]
  JP8 = Header 1 [package=1x01_offset]
  JP9 = Header 1 [package=1x01_offset]
  JP10 = Header 1 [package=1x01_offset]
  JP11 = Header 1 [package=1x01_offset]
  JP12 = Header 1 [package=1x01_offset]
  JP13 = Header 1 [package=1x01_offset]
  JP14 = Header 1 [package=1x01_offset]
  JP15 = Header 1 [package=1x01_offset]
  JP16 = Header 1 [package=1x01_offset]
  JP17 = Header 1 [package=1x01_offset]
  JP18 = Header 1 [package=1x01_offset]
  JP19 = Header 1 [package=1x01_offset]  # not connected
  JP20 = Header 1 [package=1x01_offset]
  JP21 = Header 1 [package=1x01_offset]
  JP22 = Header 1 [package=1x01_offset]
  JP23 = Header 1 [package=1x01_offset]
  JP24 = Header 1 [package=1x01_offset]
  JP25 = Header 1 [package=1x01_offset]
  JP26 = Header 1 [package=1x01_offset]
  JP27 = Header 1 [package=1x01_offset]  # not connected
  JP28 = Header 1 [package=1x01_offset]
  JP29 = Header 1 [package=1x01_offset]
  JP30 = Header 1 [package=1x01_offset]
  JP31 = Header 1 [package=1x01_offset]
  JP32 = Header 1 [package=1x01_offset]
  JP33 = Header 1 [package=1x01_offset]
  JP34 = Header 1 [package=1x01_offset]
  JP35 = Header 1 [package=1x01_offset]  # not connected
  JP36 = Header 1 [package=1x01_offset]
  JP37 = Header 1 [package=1x01_offset]
  JP38 = Header 1 [package=1x01_offset]
  JP39 = Header 1 [package=1x01_offset]
  JP40 = Header 1 [package=1x01_offset]
  JP41 = Header 1 [package=1x01_offset]
  JP42 = Header 1 [package=1x01_offset]
  JP43 = Header 1 [package=1x01_offset]
  JP44 = Header 1 [package=1x01_offset]
  JP45 = Header 1 [package=1x01_offset]
  JP46 = Header 1 [package=1x01_offset]
  JP47 = Header 1 [package=1x01_offset]
  JP48 = Header 1 [package=1x01_offset]
  JP49 = Header 1 [package=1x01_offset]
  JP50 = Header 1 [package=1x01_offset]
  JP51 = Header 1 [package=1x01_offset]
  JP52 = Header 1 [package=1x01_offset]
  JP53 = Header 1 [package=1x01_offset]
  JP54 = Header 1 [package=1x01_offset]
  JP55 = Header 1 [package=1x01_offset]
  JP56 = Header 1 [package=1x01_offset]
  JP57 = Header 1 [package=1x01_offset]
  JP58 = Header 1 [package=1x01_offset]
  JP59 = Header 1 [package=1x01_offset]
  JP60 = Header 1 [package=1x01_offset]
  JP61 = Header 1 [package=1x01_offset]
  JP62 = Header 1 [package=1x01_offset]
  JP63 = Header 1 [package=1x01_offset]
  JP64 = Header 1 [package=1x01_offset]
  JP65 = Header 1 [package=1x01_offset]
  JP66 = Header 1 [package=1x01_offset]  # not connected
  JP67 = Header 1 [package=1x01_offset]  # not connected
  JP68 = Header 1 [package=1x01_offset]  # not connected
  JP69 = Header 1 [package=1x01_offset]  # not connected
  JP70 = Header 1 [package=1x01_offset]  # not connected
  JP71 = Header 1 [package=1x01_offset]
  JP72 = Header 1 [package=1x01_offset]  # not connected
  JP73 = Header 1 [package=1x01_offset]  # not connected
  JP74 = Header 1 [package=1x01_offset]  # not connected
  JP75 = Header 1 [package=1x01_offset]  # not connected
  JP76 = Header 1 [package=1x01_offset]  # not connected
  JP77 = Header 1 [package=1x01_offset]  # not connected
  JP78 = Header 1 [package=1x01_offset]  # not connected
  JP79 = Header 1 [package=1x01_offset]
  JP80 = Header 1 [package=1x01_offset]  # not connected
  JP81 = Header 1 [package=1x01_offset]  # not connected
  JP82 = Header 1 [package=1x01_offset]  # not connected
  JP83 = Header 1 [package=1x01_offset]
  JP84 = Header 1 [package=1x01_offset]
  JP85 = Header 1 [package=1x01_offset]
  JP86 = Header 1 [package=1x01_offset]
  JP87 = Header 1 [package=1x01_offset]
  JP88 = Header 1 [package=1x01_offset]  # not connected
  JP89 = Header 1 [package=1x01_offset]
  JP90 = Header 1 [package=1x01_offset]
  JP91 = Header 1 [package=1x01_offset]
  JP92 = Header 1 [package=1x01_offset]
  JP93 = Header 1 [package=1x01_offset]  # not connected
  JP94 = Header 1 [package=1x01_offset]  # not connected
  JP95 = Header 1 [package=1x01_offset]  # not connected
  JP96 = Header 1 [package=1x01_offset]
  JP97 = Header 1 [package=1x01_offset]  # not connected
  JP98 = Header 1 [package=1x01_offset]  # not connected
  JP99 = Header 1 [package=1x01_offset]  # not connected
  JP100 = Header 1 [package=1x01_offset]  # not connected
  JP101 = Header 1 [package=1x01_offset]  # not connected
  JP102 = Header 1 [package=1x01_offset]  # not connected
  JP103 = Header 1 [package=1x01_offset]
  JP104 = Header 1 [package=1x01_offset]
  JP105 = Header 1 [package=1x01_offset]
  JP106 = Header 1 [package=1x01_offset]
  JP107 = Header 1 [package=1x01_offset]
  JP108 = Header 1 [package=1x01_offset]
  JP109 = Header 1 [package=1x01_offset]
  JP110 = Header 1 [package=1x01_offset]
  JP111 = Header 1 [package=1x01_offset]
  JP112 = Header 1 [package=1x01_offset]
  JP113 = Header 1 [package=1x01_offset]  # not connected
  JP114 = Header 1 [package=1x01_offset]  # not connected

nets:
  N1: JP5.1, JP20.1
  N2: JP6.1, JP21.1
  N3: JP7.1, JP22.1
  N4: JP8.1, JP23.1
  N5: JP9.1, JP103.1
  N6: JP10.1, JP25.1
  N7: JP11.1, JP26.1
  N8: JP12.1, JP28.1
  N9: JP13.1, JP29.1
  N10: JP14.1, JP105.1
  N11: JP15.1, JP31.1
  N12: JP16.1, JP32.1
  N13: JP17.1, JP33.1
  N14: JP18.1, JP34.1
  N15: JP24.1, JP104.1
  N16: JP30.1, JP106.1
  N17: JP36.1, JP51.1
  N18: JP37.1, JP52.1
  N19: JP38.1, JP53.1
  N20: JP39.1, JP54.1
  N21: JP40.1, JP55.1
  N22: JP41.1, JP56.1
  N23: JP42.1, JP57.1
  N24: JP43.1, JP58.1
  N25: JP44.1, JP59.1
  N26: JP45.1, JP60.1
  N27: JP46.1, JP61.1
  N28: JP47.1, JP62.1
  N29: JP48.1, JP63.1
  N30: JP49.1, JP64.1
  N31: JP50.1, JP65.1
  N32: JP71.1, JP79.1, JP96.1
  N33: JP83.1, JP107.1, JP108.1
  N34: JP84.1, JP85.1
  N35: JP86.1, JP87.1
  N36: JP89.1, JP110.1
  N37: JP90.1, JP109.1
  N38: JP91.1, JP111.1
  N39: JP92.1, JP112.1
