# Fritzing sketch shift_stepper_alt_4c_modX (saved by Fritzing 0.9.6b)
perfboards: 1

parts:
  IC3 = ULN2003A [package="DIP16 [THT]"]
  IC1 = 74HC595 [package="DIP16 [THT]"]
  IC2 = 74HC595 [package="DIP16 [THT]"]
  JP2 = Header 1 [package=1x01_offset]
  JP3 = Header 1 [package=1x01_offset]
  JP4 = Header 1 [package=1x01_offset]
  JP5 = Header 1 [package=1x01_offset]
  JP6 = Header 1 [package=1x01_offset]
  JP7 = Header 1 [package=1x01_offset]
  JP8 = Header 1 [package=1x01_offset]
  JP9 = Header 1 [package=1x01_offset]
  JP10 = Header 1 [package=1x01_offset]
  JP11 = Header 1 [package=1x01_offset]
  JP14 = Header 1 [package=1x01_offset]
  JP15 = Header 1 [package=1x01_offset]
  JP1 = Header 1 [package=1x01_offset]
  WeMos_D1_Mini = WeMos D1 Mini
  JP16_GND = Header 1 [package=1x01_offset]
  JP17_+5V = Header 1 [package=1x01_offset]
  JP19 = Header 1 [package=1x01_offset]
  JP18 = Header 1 [package=1x01_offset]
  IC4 = ULN2003A [package="DIP16 [THT]"]
  JP12 = Header 1 [package=1x01_offset]
  JP13 = Header 1 [package=1x01_offset]
  JP16_GND1 = Header 1 [package=1x01_offset]
  JP16_GND2 = Header 1 [package=1x01_offset]

nets:
  N1: IC3.In_1, IC1.Q7
  N2: IC3.In_2, IC1.Q6
  N3: IC3.In_3, IC1.Q5
  N4: IC3.In_4, IC1.Q4
  N5: IC3.In_5, IC1.Q3
  N6: IC3.In_6, IC1.Q2
  N7: IC3.In_7, IC1.Q1
  GND: IC3.0V, IC1.GND, IC1.OE, IC2.GND, IC2.OE, WeMos_D1_Mini.G, JP16_GND.1, IC4.0V, JP16_GND2.1
  VCC: IC3.COM_-_Common, IC1.MR, IC1.VCC, IC2.MR, IC2.VCC, JP6.1, JP11.1, JP1.1, JP17_+5V.1, JP18.1, IC4.COM_-_Common
  N8: IC3.Out_7, JP2.1
  N9: IC3.Out_6, JP3.1
  N10: IC3.Out_5, JP4.1
  N11: IC3.Out_4, JP5.1
  N12: IC3.Out_2, JP7.1
  N13: IC3.Out_1, JP8.1
  N14: IC1.Q7', IC2.DS
  N15: IC1.SH_CP, IC2.SH_CP, WeMos_D1_Mini.D5
  N16: IC1.ST_CP, IC2.ST_CP, WeMos_D1_Mini.D8
  N17: IC1.DS, WeMos_D1_Mini.D7
  N18: IC2.Q1, IC4.In_7
  N19: IC2.Q2, IC4.In_6
  N20: IC2.Q3, IC4.In_5
  N21: IC2.Q4, IC4.In_4
  N22: IC2.Q5, IC4.In_3
  N23: IC2.Q6, IC4.In_2
  N24: IC2.Q7, IC4.In_1
  N25: JP9.1, IC4.Out_7
  N26: JP10.1, IC4.Out_6
  N27: JP14.1, IC4.Out_2
  N28: JP15.1, IC4.Out_1
  N29: WeMos_D1_Mini.5V, JP19.1
  N30: WeMos_D1_Mini.D4, JP16_GND1.1
  N31: IC4.Out_4, JP12.1
  N32: IC4.Out_3, JP13.1
