# Fritzing sketch shift_stepper_alt_4dlc (saved by Fritzing 0.9.6b)
perfboards: 3

parts:
  IC4 = ULN2003A [package="DIP16 [THT]"]
  IC5 = ULN2003A [package="DIP16 [THT]"]
  U6 = 74HC595 [package="DIP16 [THT]"]
  U7 = 74HC595 [package="DIP16 [THT]"]
  JP4 = Header 1 [package=1x01_offset]
  JP5 = Header 1 [package=1x01_offset]
  JP6 = Header 1 [package=1x01_offset]
  JP7 = Header 1 [package=1x01_offset]
  JP8 = Header 1 [package=1x01_offset]
  JP9 = Header 1 [package=1x01_offset]
  JP10 = Header 1 [package=1x01_offset]
  JP11 = Header 1 [package=1x01_offset]
  JP12 = Header 1 [package=1x01_offset]
  JP13 = Header 1 [package=1x01_offset]
  JP14 = Header 1 [package=1x01_offset]
  JP15 = Header 1 [package=1x01_offset]
  JP16 = Header 1 [package=1x01_offset]
  JP17 = Header 1 [package=1x01_offset]
  JP18 = Header 1 [package=1x01_offset]
  JP19 = Header 1 [package=1x01_offset]
  WeMos_D1_Mini2 = WeMos D1 Mini
  JP20 = Header 1 [package=1x01_offset]
  JP21 = Header 1 [package=1x01_offset]
  JP22 = Header 1 [package=1x01_offset]
  JP23 = Header 1 [package=1x01_offset]
  JP25 = Header 1 [package=1x01_offset]
  JP26 = Header 1 [package=1x01_offset]
  JP24 = Header 1 [package=1x01_offset]
  JP27 = Header 1 [package=1x01_offset]
  JP28 = Header 1 [package=1x01_offset]
  JP29 = Header 1 [package=1x01_offset]
  JP30 = Header 1 [package=1x01_offset]
  R1 = Resistor [tolerance=±5% power=0.25 resistance=220 package=THT]
  JP35 = Header 1 [package=1x01_offset]
  JP36 = Header 1 [package=1x01_offset]
  JP38 = Header 1 [package=1x01_offset]
  JP39 = Header 1 [package=1x01_offset]
  JP40 = Header 1 [package=1x01_offset]
  JP41 = Header 1 [package=1x01_offset]
  JP42 = Header 1 [package=1x01_offset]
  JP43 = Header 1 [package=1x01_offset]
  JP44 = Header 1 [package=1x01_offset]  # not connected
  JP45 = Header 1 [package=1x01_offset]
  JP46 = Header 1 [package=1x01_offset]
  JP47 = Header 1 [package=1x01_offset]
  JP48 = Header 1 [package=1x01_offset]
  JP49 = Header 1 [package=1x01_offset]  # not connected
  JP50 = Header 1 [package=1x01_offset]
  JP51 = Header 1 [package=1x01_offset]
  JP52 = Header 1 [package=1x01_offset]
  JP53 = Header 1 [package=1x01_offset]
  JP54 = Header 1 [package=1x01_offset]
  JP55 = Header 1 [package=1x01_offset]
  JP56 = Header 1 [package=1x01_offset]
  JP57 = Header 1 [package=1x01_offset]
  JP58 = Header 1 [package=1x01_offset]
  JP59 = Header 1 [package=1x01_offset]  # not connected
  JP60 = Header 1 [package=1x01_offset]
  JP61 = Header 1 [package=1x01_offset]
  JP62 = Header 1 [package=1x01_offset]  # not connected
  JP63 = Header 1 [package=1x01_offset]
  JP64 = Header 1 [package=1x01_offset]
  JP65 = Header 1 [package=1x01_offset]  # not connected
  JP66 = Header 1 [package=1x01_offset]
  JP67 = Header 1 [package=1x01_offset]
  JP68 = Header 1 [package=1x01_offset]
  JP69 = Header 1 [package=1x01_offset]
  JP70 = Header 1 [package=1x01_offset]  # not connected
  JP71 = Header 1 [package=1x01_offset]
  JP72 = Header 1 [package=1x01_offset]
  JP73 = Header 1 [package=1x01_offset]
  JP74 = Header 1 [package=1x01_offset]
  JP75 = Header 1 [package=1x01_offset]
  JP76 = Header 1 [package=1x01_offset]
  JP77 = Header 1 [package=1x01_offset]
  JP78 = Header 1 [package=1x01_offset]
  JP79 = Header 1 [package=1x01_offset]
  JP80 = Header 1 [package=1x01_offset]
  JP81 = Header 1 [package=1x01_offset]
  JP82 = Header 1 [package=1x01_offset]
  JP83 = Header 1 [package=1x01_offset]
  JP84 = Header 1 [package=1x01_offset]
  JP85 = Header 1 [package=1x01_offset]
  JP86 = Header 1 [package=1x01_offset]
  JP87 = Header 1 [package=1x01_offset]
  JP88 = Header 1 [package=1x01_offset]
  JP89 = Header 1 [package=1x01_offset]
  JP90 = Header 1 [package=1x01_offset]
  JP91 = Header 1 [package=1x01_offset]
  JP92 = Header 1 [package=1x01_offset]
  JP93 = Header 1 [package=1x01_offset]
  JP94 = Header 1 [package=1x01_offset]
  JP95 = Header 1 [package=1x01_offset]
  JP96 = Header 1 [package=1x01_offset]
  JP97 = Header 1 [package=1x01_offset]
  JP98 = Header 1 [package=1x01_offset]
  JP99 = Header 1 [package=1x01_offset]
  JP100 = Header 1 [package=1x01_offset]
  JP101 = Header 1 [package=1x01_offset]  # not connected
  JP102 = Header 1 [package=1x01_offset]  # not connected
  JP103 = Header 1 [package=1x01_offset]  # not connected
  JP104 = Header 1 [package=1x01_offset]  # not connected
  JP105 = Header 1 [package=1x01_offset]  # not connected
  JP106 = Header 1 [package=1x01_offset]  # not connected
  JP107 = Header 1 [package=1x01_offset]  # not connected
  JP108 = Header 1 [package=1x01_offset]  # not connected
  JP109 = Header 1 [package=1x01_offset]  # not connected
  JP110 = Header 1 [package=1x01_offset]  # not connected
  JP111 = Header 1 [package=1x01_offset]  # not connected
  JP112 = Header 1 [package=1x01_offset]  # not connected
  JP113 = Header 1 [package=1x01_offset]  # not connected
  JP114 = Header 1 [package=1x01_offset]  # not connected
  JP115 = Header 1 [package=1x01_offset]  # not connected
  JP116 = Header 1 [package=1x01_offset]  # not connected
  JP117 = Header 1 [package=1x01_offset]  # not connected
  JP118 = Header 1 [package=1x01_offset]  # not connected
  JP119 = Header 1 [package=1x01_offset]  # not connected
  JP120 = Header 1 [package=1x01_offset]  # not connected
  JP121 = Header 1 [package=1x01_offset]  # not connected
  JP122 = Header 1 [package=1x01_offset]  # not connected
  JP123 = Header 1 [package=1x01_offset]  # not connected
  JP124 = Header 1 [package=1x01_offset]  # not connected
  JP125 = Header 1 [package=1x01_offset]  # not connected
  JP126 = Header 1 [package=1x01_offset]
  JP127 = Header 1 [package=1x01_offset]  # not connected
  JP128 = Header 1 [package=1x01_offset]
  JP129 = Header 1 [package=1x01_offset]
  JP130 = Header 1 [package=1x01_offset]
  JP131 = Header 1 [package=1x01_offset]
  JP132 = Header 1 [package=1x01_offset]
  JP133 = Header 1 [package=1x01_offset]  # not connected
  JP134 = Header 1 [package=1x01_offset]  # not connected
  JP135 = Header 1 [package=1x01_offset]  # not connected
  R2 = Resistor [tolerance=±5% power=0.25 resistance=220 package=THT]  # not connected
  JP136 = Header 1 [package=1x01_offset]
  JP137 = Header 1 [package=1x01_offset]
  JP138 = Header 1 [package=1x01_offset]
  JP139 = Header 1 [package=1x01_offset]  # not connected
  JP140 = Header 1 [package=1x01_offset]
  JP141 = Header 1 [package=1x01_offset]
  JP142 = Header 1 [package=1x01_offset]  # not connected
  JP143 = Header 1 [package=1x01_offset]
  JP144 = Header 1 [package=1x01_offset]
  JP145 = Header 1 [package=1x01_offset]  # not connected
  JP146 = Header 1 [package=1x01_offset]
  JP147 = Header 1 [package=1x01_offset]
  JP148 = Header 1 [package=1x01_offset]  # not connected
  R3 = Resistor [tolerance=±5% power=0.25 resistance=10k package=THT]
  R4 = Resistor [tolerance=±5% power=0.25 resistance=10k package=THT]  # not connected
  JP149 = Header 1 [package=1x01_offset]
  JP150 = Header 1 [package=1x01_offset]
  JP151 = Header 1 [package=1x01_offset]
  JP152 = Header 1 [package=1x01_offset]
  JP153 = Header 1 [package=1x01_offset]
  JP154 = Header 1 [package=1x01_offset]

nets:
  N1: IC4.In_1, U6.Q7
  N2: IC4.In_2, U6.Q6
  N3: IC4.In_3, U6.Q5
  N4: IC4.In_4, U6.Q4
  N5: IC4.In_5, U6.Q3
  N6: IC4.In_6, U6.Q2
  N7: IC4.In_7, U6.Q1
  GND: IC4.0V, IC5.0V, U6.GND, U6.OE, U7.GND, U7.OE, JP18.1, WeMos_D1_Mini2.G, JP23.1, JP26.1, JP28.1, JP36.1, R3.Pin_1, JP152.1
  VCC: IC4.COM_-_Common, IC5.COM_-_Common, U6.MR, U6.VCC, U7.MR, U7.VCC, JP8.1, JP13.1, JP19.1, JP21.1, JP25.1, JP38.1
  N8: IC4.Out_7, JP4.1
  N9: IC4.Out_6, JP5.1
  N10: IC4.Out_5, JP6.1
  N11: IC4.Out_4, JP7.1
  N12: IC4.Out_2, JP9.1
  N13: IC4.Out_1, JP10.1
  N14: IC5.In_1, U7.Q7
  N15: IC5.In_2, U7.Q6
  N16: IC5.In_3, U7.Q5
  N17: IC5.In_4, U7.Q4
  N18: IC5.In_5, U7.Q3
  N19: IC5.In_6, U7.Q2
  N20: IC5.In_7, U7.Q1
  N21: IC5.Out_7, JP11.1
  N22: IC5.Out_6, JP12.1
  N23: IC5.Out_4, JP14.1
  N24: IC5.Out_3, JP15.1
  N25: IC5.Out_2, JP16.1
  N26: IC5.Out_1, JP17.1
  N27: U6.Q7', U7.DS
  N28: U6.SH_CP, U7.SH_CP, WeMos_D1_Mini2.D5
  N29: U6.ST_CP, U7.ST_CP, WeMos_D1_Mini2.D8
  N30: U6.DS, WeMos_D1_Mini2.D7
  N31: U6.Q0, R1.Pin_1
  N32: WeMos_D1_Mini2.3V3, JP27.1, JP151.1
  N33: WeMos_D1_Mini2.5V, JP20.1
  N34: WeMos_D1_Mini2.A0, JP153.1
  N35: WeMos_D1_Mini2.D0, WeMos_D1_Mini2.RST
  N36: WeMos_D1_Mini2.D1, JP29.1
  N37: WeMos_D1_Mini2.D2, JP30.1
  N38: WeMos_D1_Mini2.D3, JP24.1
  N39: WeMos_D1_Mini2.D4, JP22.1
  N40: R1.Pin_0, JP35.1, R3.Pin_0
  N41: JP39.1, JP54.1
  N42: JP40.1, JP55.1
  N43: JP41.1, JP56.1
  N44: JP42.1, JP57.1
  N45: JP43.1, JP58.1
  N46: JP45.1, JP60.1
  N47: JP46.1, JP61.1
  N48: JP47.1, JP63.1
  N49: JP48.1, JP64.1
  N50: JP50.1, JP66.1
  N51: JP51.1, JP67.1
  N52: JP52.1, JP68.1
  N53: JP53.1, JP69.1
  N54: JP71.1, JP86.1
  N55: JP72.1, JP87.1
  N56: JP73.1, JP88.1
  N57: JP74.1, JP89.1
  N58: JP75.1, JP90.1
  N59: JP76.1, JP91.1
  N60: JP77.1, JP92.1
  N61: JP78.1, JP93.1
  N62: JP79.1, JP94.1
  N63: JP80.1, JP95.1
  N64: JP81.1, JP96.1
  N65: JP82.1, JP97.1
  N66: JP83.1, JP98.1
  N67: JP84.1, JP99.1
  N68: JP85.1, JP100.1
  N69: JP126.1, JP154.1
  N70: JP128.1, JP147.1
  N71: JP129.1, JP136.1
  N72: JP130.1, JP137.1
  N73: JP131.1, JP138.1
  N74: JP132.1, JP146.1
  N75: JP140.1, JP141.1
  N76: JP143.1, JP149.1
  N77: JP144.1, JP150.1
