# Fritzing sketch shift_stepper_alt_4x (saved by Fritzing 0.9.6b)
perfboards: 1

parts:
  U6 = 74HC595 [package="DIP16 [THT]"]
  U7 = 74HC595 [package="DIP16 [THT]"]

nets:
  N1: U6.Q7', U7.DS
  N2: U6.SH_CP, U7.SH_CP
  N3: U6.ST_CP, U7.ST_CP
