# Fritzing sketch shift_stepper_demo (saved by Fritzing 0.9.6b)
breadboards: 2

parts:
  IC1 = ULN2003A [package="DIP16 [THT]"]  # not connected
  IC2 = ULN2003A [package="DIP16 [THT]"]  # not connected
  U2 = 74HC595 [package="DIP16 [THT]"]
  U3 = 74HC595 [package="DIP16 [THT]"]
  LED1 = LED - 5mm [color="Red (633nm)" current=0.030 package="5 mm [THT]"]
  R1 = Resistor [tolerance=±5% power=0.25 resistance=220 package=THT]
  R2 = Resistor [tolerance=±5% power=0.25 resistance=220 package=THT]
  R3 = Resistor [tolerance=±5% power=0.25 resistance=220 package=THT]
  R4 = Resistor [tolerance=±5% power=0.25 resistance=220 package=THT]
  R5 = Resistor [tolerance=±5% power=0.25 resistance=220 package=THT]
  R6 = Resistor [tolerance=±5% power=0.25 resistance=220 package=THT]
  R7 = Resistor [tolerance=±5% power=0.25 resistance=220 package=THT]
  R8 = Resistor [tolerance=±5% power=0.25 resistance=220 package=THT]
  R9 = Resistor [tolerance=±5% power=0.25 resistance=220 package=THT]
  R10 = Resistor [tolerance=±5% power=0.25 resistance=220 package=THT]
  R11 = Resistor [tolerance=±5% power=0.25 resistance=220 package=THT]
  R12 = Resistor [tolerance=±5% power=0.25 resistance=220 package=THT]
  R13 = Resistor [tolerance=±5% power=0.25 resistance=220 package=THT]
  R14 = Resistor [tolerance=±5% power=0.25 resistance=220 package=THT]
  R15 = Resistor [tolerance=±5% power=0.25 resistance=220 package=THT]
  R16 = Resistor [tolerance=±5% power=0.25 resistance=220 package=THT]
  LED2 = LED - 5mm [color="Red (633nm)" current=0.030 package="5 mm [THT]"]
  LED3 = LED - 5mm [color="Red (633nm)" current=0.030 package="5 mm [THT]"]
  LED4 = LED - 5mm [color="Red (633nm)" current=0.030 package="5 mm [THT]"]
  LED5 = LED - 5mm [color="Orange (620nm)" current=0.030 package="5 mm [THT]"]
  LED6 = LED - 5mm [color="Orange (620nm)" current=0.030 package="5 mm [THT]"]
  LED7 = LED - 5mm [color="Orange (620nm)" current=0.030 package="5 mm [THT]"]
  LED8 = LED - 5mm [color="Yellow (595nm)" current=0.030 package="5 mm [THT]"]
  LED9 = LED - 5mm [color="Yellow (595nm)" current=0.030 package="5 mm [THT]"]
  LED10 = LED - 5mm [color="Yellow (595nm)" current=0.030 package="5 mm [THT]"]
  LED11 = LED - 5mm [color="Green (560nm)" current=0.030 package="5 mm [THT]"]
  LED12 = LED - 5mm [color="Green (560nm)" current=0.030 package="5 mm [THT]"]
  LED13 = LED - 5mm [color="Green (560nm)" current=0.030 package="5 mm [THT]"]
  LED14 = LED - 5mm [color="Blue (430nm)" current=0.030 package="5 mm [THT]"]
  LED15 = LED - 5mm [color="Blue (430nm)" current=0.030 package="5 mm [THT]"]
  LED16 = LED - 5mm [color="Blue (430nm)" current=0.030 package="5 mm [THT]"]
  WeMos_D1_Mini1 = WeMos D1 Mini

nets:
  N1: U2.Q1, LED7.anode
  N2: U2.Q2, LED6.anode
  N3: U2.Q3, LED5.anode
  N4: U2.Q4, LED4.anode
  N5: U2.Q5, LED3.anode
  N6: U2.Q6, LED2.anode
  N7: U2.Q7, LED1.anode
  GND: U2.GND, U2.OE, U3.GND, U3.OE, R1.Pin_1, R2.Pin_1, R3.Pin_1, R4.Pin_1, R5.Pin_1, R6.Pin_1, R7.Pin_1, R8.Pin_1, R9.Pin_1, R10.Pin_1, R11.Pin_1, R12.Pin_1, R13.Pin_1, R14.Pin_1, R15.Pin_1, R16.Pin_1, WeMos_D1_Mini1.G
  VCC: U2.MR, U2.VCC, U3.MR, U3.VCC, WeMos_D1_Mini1.5V
  N8: U2.SH_CP, U3.SH_CP, WeMos_D1_Mini1.D5
  N9: U2.ST_CP, U3.ST_CP, WeMos_D1_Mini1.D8
  N10: U2.DS, U3.Q7'
  N11: U2.Q0, LED8.anode
  N12: U3.Q1, LED15.anode
  N13: U3.Q2, LED14.anode
  N14: U3.Q3, LED13.anode
  N15: U3.Q4, LED12.anode
  N16: U3.Q5, LED11.anode
  N17: U3.Q6, LED10.anode
  N18: U3.Q7, LED9.anode
  N19: U3.DS, WeMos_D1_Mini1.D7
  N20: U3.Q0, LED16.anode
  N21: LED1.cathode, R1.Pin_0
  N22: R2.Pin_0, LED2.cathode
  N23: R3.Pin_0, LED3.cathode
  N24: R4.Pin_0, LED4.cathode
  N25: R5.Pin_0, LED5.cathode
  N26: R6.Pin_0, LED6.cathode
  N27: R7.Pin_0, LED7.cathode
  N28: R8.Pin_0, LED8.cathode
  N29: R9.Pin_0, LED9.cathode
  N30: R10.Pin_0, LED10.cathode
  N31: R11.Pin_0, LED11.cathode
  N32: R12.Pin_0, LED12.cathode
  N33: R13.Pin_0, LED13.cathode
  N34: R14.Pin_0, LED14.cathode
  N35: R15.Pin_0, LED15.cathode
  N36: R16.Pin_0, LED16.cathode
