# Fritzing sketch single_reset (saved by Fritzing 1.0.1rc)
breadboards: 1

parts:
  WeMos_D1_Mini1 = WeMos D1 Mini  # not connected
  S3 = Pushbutton [package="[THT]"]
  Q1 = TRANSISTOR_NPN [package=to-92]
  C2 = Electrolytic Capacitor [capacitance=0.47µF voltage=6.3V package="100 mil [THT, electrolytic]"]
  R2 = Resistor [tolerance=±5% power=0.25 resistance=220 package=THT]
  R3 = Resistor [tolerance=±5% power=0.25 resistance=220 package=THT]

nets:
  N1: S3.Pin_1, S3.Pin_2, Q1.C
  N2: S3.Pin_3, S3.Pin_4, R3.Pin_1
  N3: Q1.E, C2.-, R2.Pin_1
  N4: Q1.B, R3.Pin_0
