# Fritzing sketch single_reset_s (saved by Fritzing 1.0.1rc)
breadboards: 1

parts:
  WeMos_D1_Mini1 = WeMos D1 Mini
  S1 = Pushbutton [package="[THT]"]
  Q1 = TRANSISTOR_NPN [package=to-92]
  C1 = Electrolytic Capacitor [capacitance=0.47µF voltage=6.3V package="100 mil [THT, electrolytic]"]
  R1 = Resistor [tolerance=±5% power=0.25 resistance=220 package=THT]
  R2 = Resistor [tolerance=±5% power=0.25 resistance=220 package=THT]
  D1 = Schottky Diode [part_number=1N5817 package="300 mil [THT]"]
  D2 = Schottky Diode [part_number=1N5817 package="300 mil [THT]"]

nets:
  N1: WeMos_D1_Mini1.3V3, S1.Pin_3, S1.Pin_4
  N2: WeMos_D1_Mini1.D1, R2.Pin_0
  N3: WeMos_D1_Mini1.G, Q1.E
  N4: S1.Pin_1, S1.Pin_2, R1.Pin_0
  N5: Q1.B, R1.Pin_1
  N6: Q1.C, C1.-, D2.cathode
  N7: C1.+, D1.cathode
  N8: R2.Pin_1, D1.anode, D2.anode
