# Fritzing sketch overview (saved by Fritzing 0.9.3b)
breadboards: 1
stripboards: 2

parts:
  Деталь1 = Arduino Nano (Rev3.0)
  R1 = Temperature Sensor (Thermistor) [thermistor_type=NTC package=THT]
  R2 = Resistor [tolerance=±5% resistance=10k package="0603 [SMD]"]
  U2 = Hirose DF13 Series Header [part_number=DF13A-3P-1.25H package=DF13A-3P-1.25H]
  U3 = Hirose DF13 Series Header [part_number=DF13A-3P-1.25H package=DF13A-3P-1.25H]
  U4 = Hirose DF13 Series Header [part_number=DF13A-3P-1.25H package=DF13A-3P-1.25H]  # not connected

nets:
  N1: Деталь1.GND, R1.pin_0, U2.1
  N2: Деталь1.5V, R2.Pin_0, U2.2
  N3: Деталь1.A5, R1.pin_1, R2.Pin_1
  N4: Деталь1.A1, U3.3
  N5: Деталь1.A0, U2.3

notes:
  Mr. Thermistor :)
  Wago 222-415
  To soil sensors
