# Fritzing sketch thermistor-board (saved by Fritzing 0.9.3b)
breadboards: 1

parts:
  R3 = Temperature Sensor (Thermistor) [thermistor_type=NTC package=THT]
  R4 = Resistor [tolerance=±5% resistance=10k package="0603 [SMD]"]
  R6 = PHOTOCELL [package=photocell]
  R5 = Resistor [tolerance=±5% resistance=220 package="0603 [SMD]"]
  Деталь1 = Arduino Nano (Rev3.0)

nets:
  GND: R3.pin_0, R6.P$1
  N1: R3.pin_1, R4.Pin_1, Деталь1.A5
  5V: R4.Pin_0, R5.Pin_0, Деталь1.5V
  N2: R6.P$2, R5.Pin_1, Деталь1.A4
