# Fritzing sketch just_a_button (saved by Fritzing 0.9.6b)
breadboards: 1

parts:
  Деталь1 = Arduino Nano (Rev3.0)
  S1 = Momentary Switch [package=ksa_sealed_tac_switch]

nets:
  N1: Деталь1.GND, S1.3
  N2: Деталь1.D4, S1.1
  N3: Деталь1.A1, S1.4
