# Fritzing sketch schema (saved by Fritzing 0.9.3b)
breadboards: 1

parts:
  Деталь1 = Arduino Nano (Rev3.0)
  R1 = Trimmer Potentiometer [maximum_resistance=10kΩ package=THT]
  LCD1 = LCD screen
  R2 = Resistor [tolerance=±5% resistance=220 package=THT]

nets:
  GND: Деталь1.GND, R1.leg1, LCD1.VSS, LCD1.R/W
  N1: Деталь1.D2, LCD1.DB7
  N2: Деталь1.D3, LCD1.DB6
  N3: Деталь1.D4, LCD1.DB5
  N4: Деталь1.D5, LCD1.DB4
  N5: Деталь1.D11/MOSI, LCD1.E
  N6: Деталь1.D12/MISO, LCD1.V0
  5V: Деталь1.5V, R1.leg2, LCD1.VDD, LCD1.LED-, R2.Pin_0
  N7: R1.wiper, LCD1.RS
  N8: LCD1.LED+, R2.Pin_1
