# Fritzing sketch refactoring (saved by Fritzing 0.9.3b)
breadboards: 1

parts:
  Деталь1 = Arduino Nano (Rev3.0)
  R1 = Resistor [tolerance=±5% resistance=220 package=THT]
  R2 = Resistor [tolerance=±5% resistance=220 package=THT]
  R3 = Resistor [tolerance=±5% resistance=220 package=THT]
  R4 = Resistor [tolerance=±5% resistance=220 package=THT]
  R5 = Resistor [tolerance=±5% resistance=220 package=THT]
  R6 = Resistor [tolerance=±5% resistance=220 package=THT]
  R7 = Resistor [tolerance=±5% resistance=220 package=THT]
  R8 = Resistor [tolerance=±5% resistance=220 package=THT]
  LED1 = 7-SEGMENT-4DIGIT-YOUNGSUN [package=7-segment-4digit-youngsun-longpads]

nets:
  N1: Деталь1.D5, R5.Pin_0
  N2: Деталь1.D6, R6.Pin_0
  N3: Деталь1.D7, R7.Pin_0
  N4: Деталь1.D8, R8.Pin_0
  N5: Деталь1.D9, R1.Pin_0
  N6: Деталь1.D10, R2.Pin_0
  N7: Деталь1.D11/MOSI, R3.Pin_0
  N8: Деталь1.D12/MISO, R4.Pin_0
  N9: Деталь1.A3, LED1.COL-C
  N10: Деталь1.A2, LED1.C
  N11: Деталь1.A1, LED1.B
  N12: Деталь1.A0, LED1.DIG3
  N13: R1.Pin_1, LED1.F
  N14: R2.Pin_1, LED1.DIG1
  N15: R3.Pin_1, LED1.A
  N16: R4.Pin_1, LED1.G
  N17: R5.Pin_1, LED1.DIG2
  N18: R6.Pin_1, LED1.E
  N19: R7.Pin_1, LED1.COL-A
  N20: R8.Pin_1, LED1.D
