# Fritzing sketch HC-06_connection (saved by Fritzing 0.9.3b)
breadboards: 1
perfboards: 1

parts:
  R1 = Resistor [tolerance=±5% resistance=10k package="0603 [SMD]"]
  R2 = Resistor [tolerance=±5% resistance=10k package="0603 [SMD]"]
  R3 = Resistor [tolerance=±5% resistance=10k package="0603 [SMD]"]
  Деталь1 = Arduino Uno (Rev3) - ICSP

nets:
  N1: R1.Pin_0, Деталь1.D11_PWM/MOSI
  N2: R1.Pin_1, R2.Pin_0
  N3: R2.Pin_1, R3.Pin_0
  N4: R3.Pin_1, Деталь1.GND

notes:
  HC-06
  LTR: VCC, GND, TXD, RXD
  TXD is not 5V tolerant
